# Fritzing sketch projectAirQuality (saved by Fritzing 0.9.10b)
circuit board: 8.46667cm x 5.64444cm
breadboards: 1

parts:
  IC1 = DIP - 44 pins [chip_label="Pysense 2.0X" package="DIP (Dual Inline) [THT]"]
  Part2 = INA 260
  IC2 = DIP - 28 pins [chip_label=Fipy package="DIP (Dual Inline) [THT]"]
  J1 = Piezo Speaker
  LED1 = LED - 5mm [color="Red (633nm)" current=0.030 package="5 mm [THT]"]
  R1 = Resistor [tolerance=±5% resistance=220 package="2010 [SMD]"]

nets:
  N1: IC1.P0, IC2.P0
  N2: IC1.P1, IC2.P1
  GND: IC1.GND, Part2.GND, IC2.GND, J1.pin1, LED1.cathode
  5V: IC1.5V, Part2.VCC, IC2.Vin
  N3: Part2.SCL, IC2.P10
  N4: Part2.SDA, IC2.P9
  N5: IC2.P22, R1.Pin_1
  N6: IC2.P23, J1.pin2

notes:
  GND and Vin
  rails
  Pysense is used only as a programmer in this example. E.g. don't connect sensor pins/wires to it, all sensors should be connected on the breadboard and to the Fipy/Lopy4/Gpy

custom parts:
  DIP - 44 pins: A DIP stand-in part for whatever IC you want. With 44 pins on a 300mil dual inline package (DIP) footprint.
  INA 260: Rev. B, add copy
  DIP - 28 pins: A DIP stand-in part for whatever IC you want. With 28 pins on a 300mil dual inline package (DIP) footprint.
